# Fritzing sketch Schéma élec (saved by Fritzing 0.9.3b)
breadboards: 1

parts:
  Raspberry_Pi_1 = Raspberry Pi 3 [part_number=RPI-3-V1.2]
  M1 = DC Motor
  M2 = DC Motor
  M3 = DC Motor
  M4 = DC Motor
  U1 = L298 [package=multiwatt15]
  Batterie_7_4V_6800mAh = Battery Holders [package=lipo-1100mAh]
  U2 = L298 [package=multiwatt15]
  J1 = Basic Servo
  J2 = Basic Servo
  U3 = Voltage Regulator - 5V [package="DPak [SMD]"]

nets:
  N1: Raspberry_Pi_1.GPIO4, U1.IN1
  GND: Raspberry_Pi_1.GND, U1.GND, Batterie_7_4V_6800mAh.-, U2.GND, J1.gnd, J2.gnd, U3.GND
  N2: Raspberry_Pi_1.GPIO17, U1.IN2
  N3: Raspberry_Pi_1.GPIO27, U1.IN3
  N4: Raspberry_Pi_1.GPIO22, U1.IN4
  N5: Raspberry_Pi_1.GPIO5, U2.IN1
  N6: Raspberry_Pi_1.GPIO6, U2.IN2
  N7: Raspberry_Pi_1.GPIO13, J1.pulse
  N8: Raspberry_Pi_1.GPIO19, J2.pulse
  N9: Raspberry_Pi_1.GPIO26, U2.IN4
  N10: Raspberry_Pi_1.GPIO12, U1.ENA, U2.ENA
  N11: Raspberry_Pi_1.GPIO23, U2.IN3
  N12: Raspberry_Pi_1.GPIO18, U1.ENB, U2.ENB
  VCC: Raspberry_Pi_1.5V, U1.VLS, U2.VLS, J1.vcc, J2.vcc, U3.output_voltage
  N13: M1.pin_1, U1.OUT1
  N14: M1.pin_2, U1.OUT2
  N15: M2.pin_1, U1.OUT3
  N16: M2.pin_2, U1.OUT4
  N17: M3.pin_1, U2.OUT4
  N18: M3.pin_2, U2.OUT3
  N19: M4.pin_1, U2.OUT2
  N20: M4.pin_2, U2.OUT1
  N21: U1.VS, Batterie_7_4V_6800mAh.+, U2.VS, U3.input_voltage
